# Fritzing sketch music-bottle (saved by Fritzing 0.9.2b)
breadboards: 1

parts:
  MBED1 = mbed
  U1 = CAPSENSE_PAD [package=capsense_pad]
  R1 = Resistor [tolerance=±5% resistance=10k package=THT]
  R2 = Resistor [tolerance=±5% resistance=1.8k package=THT]
  R3 = Resistor [tolerance=±5% resistance=3.3k package=THT]
  R4 = Resistor [tolerance=±5% resistance=3.3k package=THT]
  R5 = Resistor [tolerance=±5% resistance=3.3k package=THT]
  R6 = Resistor [tolerance=±5% resistance=1.8k package=THT]
  R7 = Resistor [tolerance=±5% resistance=1.8k package=THT]
  R8 = Resistor [tolerance=±5% resistance=100 package=THT]
  C1 = Ceramic Capacitor [capacitance=10µF package="100 mil [THT, multilayer]"]
  Akizuki_MICRO-SD-DIP1 = Akizuki MICRO-SD-DIP
  C2 = Ceramic Capacitor [capacitance=0.01µF package="100 mil [THT, multilayer]"]
  SP1 = SPEAKER [package=pcb_mount_speaker]

nets:
  GND: MBED1.GND, U1.RES, R3.Pin_1, R4.Pin_1, R5.Pin_1, Akizuki_MICRO-SD-DIP1.GND, C2.0, SP1.+
  N1: MBED1.pin5, R6.Pin_1
  N2: MBED1.pin6, Akizuki_MICRO-SD-DIP1.MISO
  N3: MBED1.pin7, R2.Pin_1
  N4: MBED1.pin8, R7.Pin_1
  N5: MBED1.pin18, R8.Pin_1
  N6: MBED1.pin20, U1.RECEIVE, R1.Pin_1
  N7: MBED1.VU, R1.Pin_0
  N8: MBED1.VOUT, Akizuki_MICRO-SD-DIP1.VCC, C2.1
  N9: R2.Pin_0, R3.Pin_0, Akizuki_MICRO-SD-DIP1.SCK
  N10: R4.Pin_0, R6.Pin_0, Akizuki_MICRO-SD-DIP1.MOSI
  N11: R5.Pin_0, R7.Pin_0, Akizuki_MICRO-SD-DIP1.SS
  N12: R8.Pin_0, C1.1
  N13: C1.0, SP1.-

custom parts:
  Akizuki MICRO-SD-DIP: AE-MICRO-SD-DIP http://akizukidenshi.com/catalog/g/gK-05488/
